# Fritzing sketch coin_cell_temp_sensor (saved by Fritzing 0.9.2b)
circuit board: 4.46543cm x 6.02658cm
breadboards: 1

parts:
  U1 = atmega328 [package=dip]
  BAT1 = Battery Holders [package=battcon_245mm]
  Part1 = Digital Temperature Sensor Breakout - TMP102
  Part2 = NRF24L01

nets:
  N1: U1.D4, U1.AVCC, BAT1.+, Part1.V+, Part2.VCC
  N2: U1.D9_(PWM), Part2.CE
  N3: U1.D10_(PWM), Part2.CSN
  N4: U1.D11_(PWM), Part2.MOSI
  N5: U1.D12, Part2.MISO
  N6: U1.D13, Part2.SCK
  GND: U1.GND, BAT1.-, Part1.GND, Part1.ADD0, Part2.GND
  N7: U1.A4, Part1.SDA
  N8: U1.A5, Part1.SCL
